# Fritzing sketch TrailTracerFritz (saved by Fritzing 1.0.4)
breadboards: 1

parts:
  U1 = LIPO-1000mAh [package=lipo-1000]
  Part1 = 12 NeoPixel Ring [part_number=1643]
  Part2 = Adafruit PA1010D Mini GPS Module [part_number="Adafruit #4415"]
  Part3 = InvenSense MPU6050
  J1 = Screw terminal - 2 pins [package=THT]
  Boron1 = Particle Boron
  OLED_I2C1 = OLED 128x64 I2C Monochrome Display

nets:
  N1: U1.+, Boron1.LI+
  N2: U1.-, J1.pin1
  N3: Part1.IN, Boron1.D2
  VDD: Part1.VDD, Part2.VCC
  GND: Part1.GND, Part2.GND
  N4: Part2.SCL, Part3.SCL, Boron1.SCL
  N5: Part3.SDA, Boron1.SDA
  3.3V: Boron1.3.3V, OLED_I2C1.VDD
  GND_2: Boron1.GND, OLED_I2C1.GND

custom parts:
  12 NeoPixel Ring: 12 ultra bright smart LED NeoPixels are arranged in a circle with 1.5" (37mm) outer diameter. The rings are 'chainable' - connect the output pin of one to the input pin of another. Use only one microcontroller pin to control as many as you can chain together! Each LED is addressable as the driver chip is inside the LED. Each one has ~18mA constant current drive so the color will be very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
  Adafruit PA1010D Mini GPS Module: This miniature GPS breakout is only 1" x 1" (~ 25mm x 25mm) but houses a complete GPS/GNSS solution with both I2C and UART interfaces. There's even an antenna on top so it's plug and play! Support for GPS, GLONASS, GALILEO, QZSS -165 dBm sensitivity, up to 10 Hz updates Up to 210 PRN channels with 99 search channels and 33 simultaneous tracking channels 5V friendly design and only 30mA current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
  Particle Boron: The Boron LTE is a powerful LTE CAT-M1 enabled development kit that can act as either a standalone cellular device or LTE enabled gateway, repeater, or endpoint for a Particle Mesh networks. Equipped with the Nordic nRF52840 and u-blox SARA 410 processors, the Boron has built-in battery charging circuitry which makes it easier to connect a Li-Po battery and 20 mixed signal GPIOs to interface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
